# Fritzing sketch peoples_pixel (saved by Fritzing 0.9.2b)

parts:
  Part1 = Arduino Uno (Rev3)
  Raspberry_Pi1 = Raspberry Pi B rev2
  7_Segment1 = 7 Segment Display
  R1 = Resistor [tolerance=±5% resistance=330 package=THT]
  S1 = Round Pushbutton
  LED1 = LED - 5mm [color="Red (633nm)" package="5 mm [THT]"]
  R2 = Resistor [tolerance=±5% resistance=1k package=THT]  # not connected
  R3 = Resistor [tolerance=±5% resistance=1k package=THT]  # not connected

nets:
  N1: Part1.A4/SDA, Raspberry_Pi1.GPIO_2
  N2: Part1.A5/SCL, Raspberry_Pi1.GPIO_3
  N3: Part1.D8, 7_Segment1.Segment_C
  N4: Part1.D9_PWM, 7_Segment1.Segment_G
  N5: Part1.D10_PWM/SS, 7_Segment1.Segment_F
  N6: Part1.D11_PWM/MOSI, Part1.D7, 7_Segment1.common_cathode
  N7: Part1.D12/MISO, 7_Segment1.Segment_A
  N8: Part1.D13/SCK, 7_Segment1.Segment_B
  N9: Part1.D4, LED1.anode
  N10: Part1.D6_PWM, 7_Segment1.Segment_D
  N11: Part1.5V, S1.leg1
  GND: Part1.GND, Raspberry_Pi1.GND, 7_Segment1.Segment_E, R1.Pin_0
  N12: 7_Segment1.Segment_DP, R1.Pin_1

notes:
  NOT SHOWN:
  + Plug your compatable camera into the Raspberry-Pi's USB port
  + Connect your HDMI monitor to the Raspberry-Pi's HMDI port
  The example shows a segment display with pins 1 and 5 representing the common cathodes. Your display may differ. Once the common cathode pins are identified, route the remaining pins to the Arduino's digital pins 6-13, in increasing pin order.
  i.e this setup uses the following routing:
  Display pin 2 -> Uno pin 6
  Display pin 3 -> Uno pin 7
  Display pin 4 -> Uno pin 8
  Display pin 6 -> Uno pin 9
  Display pin 7 -> Uno pin 10
  Display pin 8 -> Uno pin 11
  Display pin 9 -> Uno pin 12
  Display pin 10 -> Uno pin 13
  Copyright (c) 2015 Aaron Nash
  This source file is licensed under the terms of the "GPL (v2)" license. Please see the file LICENSE.md included in this distribution for licensing terms.
